# Fritzing sketch Main_Schematic (saved by Fritzing 0.9.3b)

parts:
  WeMos_D1_Mini1 = WeMos D1 Mini
  J1 = JST-B3P-VH [part_number=JST-B3P-VH package=THT]
  J2 = JST-B3P-VH [part_number=JST-B3P-VH package=THT]
  U1 = Sharp PC817 [package=THT]
  R1 = Resistor [tolerance=±5% resistance=150 package="0603 [SMD]"]
  J3 = male pin header, 3 pins [form="♂ (male)"]  # not connected
  J4 = male pin header, 3 pins [form="♂ (male)"]

nets:
  N1: WeMos_D1_Mini1.3V3, J4.pin1
  N2: WeMos_D1_Mini1.D0, J1.pin1
  N3: WeMos_D1_Mini1.D5, U1.Pin_1
  N4: WeMos_D1_Mini1.D6, J4.pin2
  N5: WeMos_D1_Mini1.G, J1.pin3, R1.Pin_0, J4.pin3
  N6: J2.pin1, U1.Pin_4
  N7: J2.pin3, U1.Pin_3

notes:
  PwrBtn+ PwrBtn-
  ↓ ↓
  PwrLED+ PwrLED-
  ↓ ↓
